// Logisim project pisoregisteranurag.circ as structural Verilog: 1 circuit, main circuit main
module main (
  input  in_1,
  input  in_2,
  input  in_3,
  input  in_4,
  input  in_5
);

  wire clock_1_out, d_ff_1_q, d_ff_2_q, d_ff_3_q, d_ff_4_q, multiplexer_1_out, multiplexer_2_out,
       multiplexer_3_out, multiplexer_4_out;

  Clock clock_1 (.out(clock_1_out));
  Multiplexer multiplexer_1 (.in0(1'b1), .in1(in_1), .out(multiplexer_1_out), .sel(in_5));
  D_Flip_Flop d_ff_1 (.clk(clock_1_out), .D(multiplexer_1_out), .Q(d_ff_1_q));  // open: Qn, preset, reset
  Multiplexer multiplexer_2 (.in0(d_ff_1_q), .in1(in_2), .out(multiplexer_2_out), .sel(in_5));
  D_Flip_Flop d_ff_2 (.clk(clock_1_out), .D(multiplexer_2_out), .Q(d_ff_2_q));  // open: Qn, preset, reset
  Multiplexer multiplexer_3 (.in0(d_ff_2_q), .in1(in_3), .out(multiplexer_3_out), .sel(in_5));
  D_Flip_Flop d_ff_3 (.clk(clock_1_out), .D(multiplexer_3_out), .Q(d_ff_3_q));  // open: Qn, preset, reset
  Multiplexer multiplexer_4 (.in0(d_ff_3_q), .in1(in_4), .out(multiplexer_4_out), .sel(in_5));
  D_Flip_Flop d_ff_4 (.clk(clock_1_out), .D(multiplexer_4_out), .Q(d_ff_4_q));  // open: Qn, preset, reset
  // Probe on d_ff_4_q
endmodule
